# Fritzing sketch ProyekSK (saved by Fritzing 0.9.2b)
breadboards: 1

parts:
  Part1 = Arduino Uno (Rev3)
  PIR1 = PIR sensor
  J1 = Basic Servo
  Part2 = HX711 Weighing Sensor Module
  Load_Cell1 = Load Cell - Red/white/black/green
  Part3 = SRF05 Ultrasonic Rangefinder
  VCC2 = Battery block 9V
  JACK1 = 2.1mm Barrel Jack with Terminal Block
  LCD1 = LCD screen
  LCM1602_IIC1 = LCM1602 IIC [part_number="LCM1602 IIC" chip_label="LCM1602 IIC" package="DIP (Dual Inline) [THT]"]
  WATER_PUMP1 = water pump/motor  # not connected

nets:
  N1: Part1.D9_PWM, J1.pulse
  N2: Part1.D10_PWM/SS, Part2.CK/TX
  N3: Part1.D5_PWM, PIR1.SIG
  N4: Part1.D6_PWM, Part2.DO/RX
  N5: Part1.D7, Part3.Echo
  VCC: PIR1.VDD, Part2.VCC, Part3.VCC, LCM1602_IIC1.VCC
  GND: PIR1.GND, J1.gnd, Part2.GND, Part3.GND, LCM1602_IIC1.GND
  N6: Part2.E+, Load_Cell1.wire1
  N7: Part2.E-, Load_Cell1.wire3
  N8: Part2.A+, Load_Cell1.wire4
  N9: Part2.A-, Load_Cell1.wire2
  N10: VCC2.-, JACK1.NEG
  N11: VCC2.+, JACK1.POS
  VSS: LCD1.VSS, LCM1602_IIC1.VSS
  VDD: LCD1.VDD, LCM1602_IIC1.VDD
  N12: LCD1.V0, LCM1602_IIC1.V0
  N13: LCD1.RS, LCM1602_IIC1.RS
  N14: LCD1.R/W, LCM1602_IIC1.RW
  N15: LCD1.E, LCM1602_IIC1.E
  N16: LCD1.DB0, LCM1602_IIC1.D0
  N17: LCD1.DB1, LCM1602_IIC1.D1
  N18: LCD1.DB2, LCM1602_IIC1.D2
  N19: LCD1.DB3, LCM1602_IIC1.D3
  N20: LCD1.DB4, LCM1602_IIC1.D4
  N21: LCD1.DB5, LCM1602_IIC1.D5
  N22: LCD1.DB6, LCM1602_IIC1.D6
  N23: LCD1.DB7, LCM1602_IIC1.D7
  N24: LCD1.LED+, LCM1602_IIC1.A
  N25: LCD1.LED-, LCM1602_IIC1.K

notes:
  SERVO:
  Pin Y -> 9
  SENSOR PIR:
  Data -> 10
  Sensor RTC:
  SDA = SDA
  SCL = SC
  HCSR04
  Trig -> 6
  echo -> 5
  HX711

custom parts:
  HX711 Weighing Sensor Module: HX711 is a precision 24-bit analog-to-digital converter (ADC) designed for weigh scales and industrial control applications to interface directly with a bridge sensor.
  Load Cell - Red/white/black/green: A rectangle load cell/weighting pressure Sensor with four wires - Red, white, black, green. Normally corresponding with E+, E-, A+, A- respectively.
  LCM1602 IIC: I2C-Module to use a 1602 or 2004 LCD on with the wire.h libory Serial LCD Modul
  water pump/motor: WATER PUMP BY ARDUBLOCKTR
